# Fritzing sketch Adapter_ESP8266_v0.2 (saved by Fritzing 0.9.4)
circuit board: 5.09999cm x 3.39999cm
breadboards: 1

parts:
  J1 = double row female pin header, 32 pins [form="♀ (female)"]
  J2 = double row female pin header, 24 pins [form="♀ (female)"]
  A0/D17+13 = Grove 4 Digit Display
  D12+14 = Grove 4 Digit Display
  I2C = Grove 4 Digit Display
  UART = Grove 4 Digit Display
  100kΩ = Resistor [tolerance=±5% resistance=100k package=THT]

nets:
  N1: J1.pin1, J1.pin32
  VCC: J1.pin2, J1.pin31, A0/D17+13.VCC, D12+14.VCC, I2C.VCC, UART.VCC, 100kΩ.Pin_0
  N2: J1.pin3, J1.pin30
  N3: J1.pin4, J1.pin29
  N4: J1.pin5, J1.pin28, A0/D17+13.CLK
  N5: J1.pin6, J1.pin27
  N6: J1.pin7, J1.pin26
  N7: J1.pin8, J1.pin25
  N8: J1.pin9, J1.pin24
  N9: J1.pin10, J1.pin23
  N10: J1.pin11, J1.pin22
  N11: J1.pin12, J1.pin21, A0/D17+13.DIO
  N12: J1.pin13, J1.pin20
  N13: J1.pin14, J1.pin19, UART.CLK
  N14: J1.pin15, J1.pin18, UART.DIO
  N15: J1.pin16, J1.pin17, 100kΩ.Pin_1
  N16: J2.pin1, J2.pin24
  N17: J2.pin2, J2.pin23
  N18: J2.pin3, J2.pin22
  N19: J2.pin4, J2.pin21, D12+14.DIO
  N20: J2.pin5, J2.pin20, D12+14.CLK
  N21: J2.pin6, J2.pin19
  N22: J2.pin7, J2.pin18
  N23: J2.pin8, J2.pin17
  N24: J2.pin9, J2.pin16
  N25: J2.pin10, J2.pin15
  N26: J2.pin11, J2.pin14, I2C.CLK
  N27: J2.pin12, J2.pin13, I2C.DIO

notes:
  tmb.gr/iot-bricks
  Grove Adapter for
  CC BY-SA
  Feather HUZZAH
  @tamberg
  v0.2
  ESP8266
